# Fritzing sketch schematic (saved by Fritzing 0.9.6b)
breadboards: 1

parts:
  Q1 = MOSFET-NCHANNEL [package=to220v]
  J1 = Piezo Speaker
  VCC1 = Battery block 9V
  Part1 = Arduino Uno (Rev3)

nets:
  N1: Q1.G, Part1.D5_PWM
  N2: Q1.D, J1.pin1
  N3: Q1.S, VCC1.-, Part1.GND
  N4: J1.pin2, VCC1.+, Part1.VIN
